// Logisim project 1-1.circ as structural Verilog: 1 circuit, main circuit main
module main (
  input  A,
  input  B,
  output S,
  output C
);

  xor xor_1 (S, A, B);
  or or_1 (C, A, A);

  // Notes on the sheet:
  //   一位二进制半加器
endmodule
