// Logisim project 1-2.circ as structural Verilog: 1 circuit, main circuit main
module main (
  input  A,
  input  B,
  input  C,
  output S,
  output C0
);

  wire and_1_out, and_2_out, or_1_out, xor_1_out;

  and and_1 (and_1_out, A, B);
  or or_1 (or_1_out, A, B);
  xor xor_1 (xor_1_out, A, B);
  and and_2 (and_2_out, C, or_1_out);
  xor xor_2 (S, xor_1_out, C);
  or or_2 (C0, and_1_out, and_2_out);

  // Notes on the sheet:
  //   一位二进制全加器
endmodule
