// Logisim project 1-3.circ as structural Verilog: 1 circuit, main circuit main
module main (
  input  C0,
  input  A3,
  input  B3,
  input  A2,
  input  B2,
  input  A1,
  input  B1,
  input  A0,
  input  B0,
  output S3,
  output S2,
  output S1,
  output S0,
  output C4
);

  wire and_1_out, and_2_out, and_3_out, and_4_out, and_5_out, and_6_out, and_7_out, and_8_out, or_2_out,
       or_3_out, or_4_out, or_5_out, or_6_out, or_7_out, or_8_out, xor_2_out, xor_4_out, xor_6_out, xor_8_out;

  and and_1 (and_1_out, A3, B3);
  or or_1 (C4, and_1_out, and_2_out);
  and and_2 (and_2_out, or_3_out, or_2_out);
  or or_2 (or_2_out, A3, B3);
  xor xor_1 (S3, or_3_out, xor_2_out);
  xor xor_2 (xor_2_out, A3, B3);
  or or_3 (or_3_out, and_4_out, and_3_out);
  and and_3 (and_3_out, or_5_out, or_4_out);
  and and_4 (and_4_out, A2, B2);
  xor xor_3 (S2, or_5_out, xor_4_out);
  or or_4 (or_4_out, A2, B2);
  xor xor_4 (xor_4_out, A2, B2);
  or or_5 (or_5_out, and_5_out, and_6_out);
  and and_5 (and_5_out, A1, B1);
  and and_6 (and_6_out, or_7_out, or_6_out);
  or or_6 (or_6_out, A1, B1);
  xor xor_5 (S1, or_7_out, xor_6_out);
  xor xor_6 (xor_6_out, A1, B1);
  or or_7 (or_7_out, and_7_out, and_8_out);
  and and_7 (and_7_out, A0, B0);
  and and_8 (and_8_out, C0, or_8_out);
  or or_8 (or_8_out, A0, B0);
  xor xor_7 (S0, C0, xor_8_out);
  xor xor_8 (xor_8_out, A0, B0);

  // Notes on the sheet:
  //   串行进位的四位二进制并行加法器
endmodule
