// Logisim project 1-4.circ as structural Verilog: 1 circuit, main circuit main
module main (
  input  C0,
  input  A3,
  input  B3,
  input  A2,
  input  B2,
  input  A1,
  input  B1,
  input  A0,
  input  B0,
  output S3,
  output S2,
  output S1,
  output S0,
  output Co
);

  wire and_1_out, and_2_out, and_3_out, and_4_out, and_5_out, and_6_out, and_7_out, and_8_out, and_9_out,
       and_10_out, G0_out, G1_out, G2_out, G3_out, or_2_out, or_3_out, or_4_out, P0_out, P1_out, P2_out,
       P3_out;

  and and_1 (and_1_out, P3_out, P2_out, P1_out, P0_out, C0);
  and and_2 (and_2_out, P3_out, P2_out, P1_out, G0_out);
  or or_1 (Co, and_1_out, and_2_out, and_3_out, and_4_out, G3_out);
  and and_3 (and_3_out, P3_out, P2_out, G1_out);
  xor P3 (P3_out, A3, B3);
  and and_4 (and_4_out, P3_out, G2_out);
  and G3 (G3_out, A3, B3);
  and and_5 (and_5_out, P2_out, P1_out, P0_out, C0);
  xor xor_1 (S3, P3_out, or_2_out);
  and and_6 (and_6_out, P2_out, P1_out, G0_out);
  or or_2 (or_2_out, and_5_out, and_6_out, and_7_out, G2_out);
  and and_7 (and_7_out, P2_out, G1_out);
  xor P2 (P2_out, A2, B2);
  and G2 (G2_out, A2, B2);
  xor xor_2 (S2, P2_out, or_3_out);
  or or_3 (or_3_out, and_9_out, and_8_out, G1_out);
  and and_8 (and_8_out, P1_out, G0_out);
  and and_9 (and_9_out, P1_out, P0_out, C0);
  xor P1 (P1_out, A1, B1);
  and G1 (G1_out, A1, B1);
  xor xor_3 (S1, P1_out, or_4_out);
  and and_10 (and_10_out, P0_out, C0);
  xor P0 (P0_out, A0, B0);
  or or_4 (or_4_out, and_10_out, G0_out);
  and G0 (G0_out, A0, B0);
  xor xor_4 (S0, P0_out, C0);

  // Notes on the sheet:
  //   先行进位的四位二进制加法器
endmodule
