// Logisim project 1-5.circ as structural Verilog: 1 circuit, main circuit main
module main (
  input  in_1,
  input  in_2,
  input  in_3,
  input  in_4,
  input  in_5,
  input  in_6,
  input  in_7,
  input  in_8,
  input  in_9,
  output out_10,
  output out_11,
  output out_12,
  output out_13,
  output out_14
);

  // _1_4_main main_1: pin names not known; wires that end beside it: out_14, in_2, out_10, in_3, in_4, out_11, in_5, out_12, in_6, in_7, out_13, in_8, in_9, in_1

  // Notes on the sheet:
  //   封装好的先行进位的四位二进制加法器
endmodule
