// Logisim project 2-1-test.circ as structural Verilog: 1 circuit, main circuit main
module main (
  output out_1,
  output \四位二进制可逆计数器封装测试电路 ,
  output out_3,
  output out_4
);

  wire button_1_out, button_2_out, button_3_out;

  Button button_1 (.out(button_1_out));
  Button button_2 (.out(button_2_out));
  Button button_3 (.out(button_3_out));
  _2_1_main main_1 (
    .Q3(out_1), .Q2(\四位二进制可逆计数器封装测试电路 ), .Q1(out_3), .Q0(out_4), .CPD(button_3_out), .CPU(button_1_out),
    .CLR(button_2_out));
endmodule
