// Logisim project 2-1.circ as structural Verilog: 1 circuit, main circuit main
module main (
  input  CPD,
  input  CPU,
  input  CLR,
  output Q3,
  output Q2,
  output Q1,
  output Q0
);

  wire and_1_out, and_2_out, and_3_out, and_4_out, and_5_out, and_6_out, D0_qn, D1_qn, D2_qn, D3_qn,
       or_1_out, or_2_out, or_3_out, xor_1_out;

  and and_1 (and_1_out, CPD, D2_qn, D1_qn, D0_qn);
  and and_2 (and_2_out, CPU, Q2, Q1, Q0);
  and and_3 (and_3_out, CPD, D1_qn, D0_qn);
  and and_4 (and_4_out, CPU, Q1, Q0);
  and and_5 (and_5_out, CPD, D0_qn);
  and and_6 (and_6_out, CPU, Q0);
  or or_1 (or_1_out, and_1_out, and_2_out);
  or or_2 (or_2_out, and_3_out, and_4_out);
  or or_3 (or_3_out, and_5_out, and_6_out);
  xor xor_1 (xor_1_out, CPD, CPU);
  D_Flip_Flop #(.trigger("falling")) D3 (
    .clk(or_1_out), .D(D3_qn), .Q(Q3), .Qn(D3_qn), .reset(CLR));  // open: preset, en
  D_Flip_Flop #(.trigger("falling")) D2 (
    .clk(or_2_out), .D(D2_qn), .Q(Q2), .Qn(D2_qn), .reset(CLR));  // open: preset, en
  D_Flip_Flop #(.trigger("falling")) D1 (
    .clk(or_3_out), .D(D1_qn), .Q(Q1), .Qn(D1_qn), .reset(CLR));  // open: preset, en
  D_Flip_Flop #(.trigger("falling")) D0 (
    .clk(xor_1_out), .D(D0_qn), .Q(Q0), .Qn(D0_qn), .reset(CLR));  // open: preset, en

  // Notes on the sheet:
  //   四位二进制可逆计数器
endmodule
