// Logisim project 2-2.circ as structural Verilog: 1 circuit, main circuit main
module main (
  input  Q3,
  input  Q2,
  input  Q1,
  input  Q0,
  output out_5,
  output out_6,
  output out_7,
  output out_8,
  output \四位二进制数转两位8241码电路 ,
  output out_10,
  output out_11,
  output out_12
);

  wire and_1_out, or_1_out;

  and and_1 (and_1_out, or_1_out, Q3);
  or or_1 (or_1_out, Q1, Q2);
  // adder_main main_1: pin names not known; wires that end beside it: out_8, 1'b0, \四位二进制数转两位8241码电路 , and_1_out, and_1_out, out_10, 1'b0, out_11, Q3, Q2, out_12, Q1, Q0, 1'b0

  assign out_5 = 1'b0;
  assign out_6 = 1'b0;
  assign out_7 = 1'b0;
endmodule
