// Logisim project 2-3-a.circ as structural Verilog: 1 circuit, main circuit main
module main (
  input  A3,
  input  A2,
  input  A1,
  input  A0,
  output out_5,
  output out_6,
  output out_7,
  output out_8,
  output out_9,
  output out_10,
  output out_11
);

  wire A1_A0_out, A1_nA0_out, A2_A0_out, A2_A1_out, A2_nA0_out, A2_nA1_A0_out, A2_nA1_out, A3_nA1_out,
       nA1_nA0_out, nA2_A1_out, nA2_nA0_out, not_1_out, not_2_out, not_3_out, not_4_out;

  not not_1 (not_1_out, A3);
  not not_2 (not_2_out, A2);
  not not_3 (not_3_out, A1);
  not not_4 (not_4_out, A0);
  xnor A2_A0 (A2_A0_out, A2, A0);
  xnor A1_A0 (A1_A0_out, A1, A0);
  and nA2_nA0 (nA2_nA0_out, not_2_out, not_4_out);
  and A1_nA0 (A1_nA0_out, A1, not_4_out);
  and nA2_A1 (nA2_A1_out, not_2_out, A1);
  and A2_nA1_A0 (A2_nA1_A0_out, A2, not_3_out, A0);
  and nA1_nA0 (nA1_nA0_out, not_3_out, not_4_out);
  and A2_nA0 (A2_nA0_out, A2, not_4_out);
  and A2_nA1 (A2_nA1_out, A2, not_3_out);
  and A3_nA1 (A3_nA1_out, A3, not_3_out);
  xor A2_A1 (A2_A1_out, A2, A1);
  or a (out_5, A2_A0_out, A3, A1);
  or b (out_6, A1_A0_out, not_2_out);
  nand c (out_7, A1, not_1_out, not_2_out, not_4_out);
  or d (out_8, nA2_nA0_out, A1_nA0_out, A3, nA2_A1_out, A2_nA1_A0_out);
  or e (out_9, nA2_nA0_out, A1_nA0_out);
  or f (out_10, nA1_nA0_out, A2_nA0_out, A2_nA1_out, A3_nA1_out);
  or g (out_11, A1_nA0_out, A2_A1_out, A3);

  // Notes on the sheet:
  //   七段译码器
endmodule
