// Logisim project 2-3-b.circ as structural Verilog: 1 circuit, main circuit main
module main (
  input  A3,
  input  A2,
  input  A1,
  input  A0
);

  wire main_1_out_5, main_1_out_6, main_1_out_7, main_1_out_8, main_1_out_9, main_1_out_10, main_1_out_11;

  _7_Segment_Display u_7_segment_display_1 (
    .g(main_1_out_11), .f(main_1_out_10), .a(main_1_out_5), .b(main_1_out_6), .e(main_1_out_9),
    .d(main_1_out_8), .c(main_1_out_7));  // open: dp
  _2_3_a_main main_1 (
    .A3(A3), .A2(A2), .A1(A1), .A0(A0), .out_5(main_1_out_5), .out_6(main_1_out_6), .out_7(main_1_out_7),
    .out_8(main_1_out_8), .out_9(main_1_out_9), .out_10(main_1_out_10), .out_11(main_1_out_11));

  // Notes on the sheet:
  //   七段显示数码管电路
endmodule
