// Logisim project 2-4.circ as structural Verilog: 1 circuit, main circuit main
module main (
  input  \增加 ,
  input  \清零 ,
  input  \减少 ,
  output S3,
  output S2,
  output S1,
  output S1_2,
  output \报警 
);

  wire and_1_out, and_2_out, nand_1_out, or_1_out;

  nand nand_1 (nand_1_out, S3, S2, S1, S1_2);
  or or_1 (or_1_out, S3, S2, S1, S1_2);
  not not_1 (\报警 , nand_1_out);
  and and_1 (and_1_out, nand_1_out, \增加 );
  and and_2 (and_2_out, \减少 , or_1_out);
  _2_1_main main_1 (.Q3(S3), .Q2(S2), .Q1(S1), .Q0(S1_2), .CPD(and_2_out), .CPU(and_1_out), .CLR(\清零 ));

  // Notes on the sheet:
  //   门禁系统报警电路
endmodule
