// Logisim project 2-5-a.circ as structural Verilog: 1 circuit, main circuit main
module main (
  input  CPU,
  input  CLP,
  input  CPD,
  output a,
  output b,
  output c,
  output d,
  output e,
  output f,
  output g,
  output a_2,
  output b_2,
  output c_2,
  output d_2,
  output e_2,
  output f_2,
  output g_2,
  output ALARM
);

  wire main_3_out_5, main_3_out_6, main_3_out_7, main_3_out_8, main_3_out_10, main_3_out_11, main_3_out_12,
       \main_3_四位二进制数转两位8241码电路 , main_4_s1, main_4_s1_2, main_4_s2, main_4_s3;

  _2_3_a_main main_1 (
    .A3(main_3_out_5), .A2(main_3_out_6), .A1(main_3_out_7), .A0(main_3_out_8), .out_5(a), .out_6(b),
    .out_7(c), .out_8(d), .out_9(e), .out_10(f), .out_11(g));
  _2_3_a_main main_2 (
    .A3(\main_3_四位二进制数转两位8241码电路 ), .A2(main_3_out_10), .A1(main_3_out_11), .A0(main_3_out_12), .out_5(a_2),
    .out_6(b_2), .out_7(c_2), .out_8(d_2), .out_9(e_2), .out_10(f_2), .out_11(g_2));
  _2_2_main main_3 (
    .out_5(main_3_out_5), .out_6(main_3_out_6), .out_7(main_3_out_7), .out_8(main_3_out_8),
    .\四位二进制数转两位8241码电路 (\main_3_四位二进制数转两位8241码电路 ), .out_10(main_3_out_10), .out_11(main_3_out_11),
    .out_12(main_3_out_12), .Q3(main_4_s3), .Q2(main_4_s2), .Q1(main_4_s1), .Q0(main_4_s1_2));
  _2_4_main main_4 (
    .\增加 (CPU), .\清零 (CLP), .\减少 (CPD), .\报警 (ALARM), .S3(main_4_s3), .S2(main_4_s2), .S1(main_4_s1),
    .S1_2(main_4_s1_2));
endmodule
